// Logisim project battleship.circ as structural Verilog: 3 circuits, main circuit main
module main (
  input  [3:0] Alvo,
  input  [3:0] Navio1,
  input  [3:0] Navio2,
  output Acertou,
  output Errou
);

  wire button_1_out, comparator_1_eq, comparator_2_eq, or_1_out;
  wire [3:0] encoder_1_x, encoder_2_x;

  Encoder encoder_1 (.a(Navio1), .x(encoder_1_x));
  Encoder encoder_2 (.a(Navio2), .x(encoder_2_x));
  Comparator #(.width(4)) comparator_1 (.a(Alvo), .b(encoder_1_x), .eq(comparator_1_eq));  // open: gt, lt
  Comparator #(.width(4)) comparator_2 (.a(Alvo), .b(encoder_2_x), .eq(comparator_2_eq));  // open: gt, lt
  Button button_1 (.out(button_1_out));
  or or_1 (or_1_out, comparator_1_eq, comparator_2_eq);
  and and_1 (Acertou, or_1_out, button_1_out);
  and and_2 (Errou, button_1_out, ~or_1_out);  // AND_Gate
endmodule

module Encoder (
  input  [3:0] a,
  output [3:0] x
);

  wire and_1_out, and_2_out, and_3_out, and_4_out, and_5_out, and_6_out, and_7_out, and_8_out, and_9_out,
       and_10_out, and_11_out, and_12_out, and_13_out, and_14_out, and_15_out, and_16_out, not_1_out,
       not_2_out, not_3_out, not_4_out;

  not not_1 (not_1_out, a[3]);
  not not_2 (not_2_out, a[2]);
  not not_3 (not_3_out, a[1]);
  not not_4 (not_4_out, a[0]);
  and and_1 (and_1_out, not_1_out, not_2_out, a[0]);
  and and_2 (and_2_out, not_1_out, a[2], not_4_out);
  and and_3 (and_3_out, a[3], a[1], not_4_out);
  and and_4 (and_4_out, a[3], not_3_out, a[0]);
  and and_5 (and_5_out, not_1_out, not_2_out, not_4_out);
  and and_6 (and_6_out, not_1_out, a[1], a[0]);
  and and_7 (and_7_out, not_1_out, a[2], not_3_out);
  and and_8 (and_8_out, a[3], a[1], not_4_out);
  and and_9 (and_9_out, not_1_out, a[0]);
  and and_10 (and_10_out, a[1], a[0]);
  and and_11 (and_11_out, a[2], a[0]);
  and and_12 (and_12_out, not_1_out, a[2], not_3_out);
  and and_13 (and_13_out, not_2_out, a[1]);
  and and_14 (and_14_out, not_1_out, a[1], not_4_out);
  and and_15 (and_15_out, a[2], not_3_out, a[0]);
  and and_16 (and_16_out, a[3], a[2], not_3_out);
  or or_1 (x[3], and_1_out, and_2_out, and_3_out, and_4_out);
  or or_2 (x[2], and_5_out, and_6_out, and_7_out, and_8_out);
  or or_3 (x[1], and_9_out, and_10_out, and_11_out, and_12_out);
  or or_4 (x[0], and_13_out, and_14_out, and_15_out, and_16_out);
endmodule

module Decodificador (
  input  [3:0] a,
  output [3:0] x
);

  wire and_1_out, and_2_out, and_3_out, and_4_out, and_5_out, and_6_out, and_7_out, and_8_out, and_9_out,
       and_10_out, and_11_out, and_12_out, and_13_out, and_14_out, and_15_out, and_16_out, and_17_out,
       and_18_out, not_1_out, not_2_out, not_3_out, not_4_out;

  not not_1 (not_1_out, a[3]);
  not not_2 (not_2_out, a[2]);
  not not_3 (not_3_out, a[1]);
  not not_4 (not_4_out, a[0]);
  and and_1 (and_1_out, not_1_out, not_2_out);
  and and_2 (and_2_out, not_2_out, a[1], a[0]);
  and and_3 (and_3_out, a[3], a[2], not_3_out);
  and and_4 (and_4_out, not_2_out, not_3_out, not_4_out);
  and and_5 (and_5_out, not_2_out, not_3_out, a[0]);
  and and_6 (and_6_out, not_1_out, a[1], not_4_out);
  and and_7 (and_7_out, not_1_out, a[2], a[1]);
  and and_8 (and_8_out, a[3], not_2_out, a[1]);
  and and_9 (and_9_out, a[3], a[2], not_3_out);
  and and_10 (and_10_out, not_1_out, not_2_out, a[1]);
  and and_11 (and_11_out, not_1_out, a[1], not_4_out);
  and and_12 (and_12_out, a[2], not_3_out, a[0]);
  and and_13 (and_13_out, a[3], not_3_out, a[0]);
  and and_14 (and_14_out, a[3], a[2], not_3_out);
  and and_15 (and_15_out, a[3], a[2], a[0]);
  and and_16 (and_16_out, not_1_out, a[1]);
  and and_17 (and_17_out, a[1], a[0]);
  or or_1 (x[0], and_16_out, and_17_out, and_18_out);
  and and_18 (and_18_out, a[3], not_2_out, not_4_out);
  or or_2 (x[3], and_1_out, and_2_out, and_3_out, and_4_out);
  or or_3 (x[2], and_5_out, and_6_out, and_7_out, and_8_out, and_9_out);
  or or_4 (x[1], and_10_out, and_11_out, and_12_out, and_13_out, and_14_out, and_15_out);
endmodule
